# Fritzing sketch fritzing (saved by Fritzing 0.8.7b)
breadboards: 1

parts:
  IR = IR Receiver Breakout [package=PCB]
  KY-1 = Keyes Relay [package=THT]
  KY-2 = Keyes Relay [package=THT]
  KY-3 = Keyes Relay [package=THT]
  220v_AC_FAN = Fan - 4 wire [package=THT]
  Eleman1 = Arduino Uno (Rev3)
  5V = 4 x AAA Battery Mount
  R1 = Resistor [tolerance=±5% resistance=220 package=THT]
  R2 = Resistor [tolerance=±5% resistance=220 package=THT]
  RGB_LED = RGB LED (com. anode, rbg) [package="5 mm [THT]"]  # not connected
  R3 = Resistor [tolerance=±5% resistance=220 package=THT]

nets:
  GND: IR.GND, KY-1.ground, KY-2.ground, Eleman1.GND
  N1: IR.OUT, KY-1.power, KY-2.power, KY-3.power, Eleman1.5V, 5V.+
  N2: IR.VCC, Eleman1.D2
  N3: KY-1.signal, Eleman1.D4
  N4: KY-1.NO, 220v_AC_FAN.PWM
  N5: KY-2.signal, Eleman1.D3_PWM
  N6: KY-2.NO, 220v_AC_FAN.Tach
  N7: KY-3.signal, Eleman1.D5_PWM
  N8: KY-3.NO, 220v_AC_FAN.Power
  N9: Eleman1.D9_PWM, R2.Pin_1
  N10: Eleman1.D10_PWM/SS, R3.Pin_1
  N11: Eleman1.D6_PWM, R1.Pin_1

notes:
  FOR MY FAN
  RED=HIGH SPEED
  WHITE= MEDIUM SPEED
  BLUE=LOW SPEED
  YOU NEED TO FIND WHICH CABLE GIVES WHICH SPEED
  AC POWER 220V
  I USED 2 CHANNEL RELAY + ONE CHANNEL RELAY

custom parts:
  Keyes Relay: The Keyes 5V relay module is suitable for SCM development, home appliance control. It uses a 5V~12V TIL control signal which can control DC / AC signal.
  Fan - 4 wire: Fan, 4 wire with tach.
